// Digital circuit Program_Counter.dig as structural Verilog
module Program_Counter (
  input  CLK,
  input  [3:0] A0,
  input  [3:0] B0,
  input  [3:0] A1,
  input  [3:0] B2,
  input  [3:0] A2,
  input  [3:0] B2_2,
  input  [3:0] A3,
  input  [3:0] B3,
  input  Control,
  output [3:0] Output
);

  wire [3:0] and_1_out, and_2_out, and_3_out, and_4_out, and_5_out, and_6_out, and_7_out, multiplexer_1_out,
       or_1_out, or_2_out, or_3_out, or_4_out, xor_1_out, xor_2_out, xor_3_out, xor_4_out, xor_5_out,
       xor_6_out, xor_7_out;

  assign and_1_out = A0 & B0;  // And and_1, 4 bits wide
  assign xor_1_out = A1 ^ B2;  // XOr xor_1, 4 bits wide
  assign and_2_out = B2 & A1;  // And and_2, 4 bits wide
  assign xor_2_out = A2 ^ B2_2;  // XOr xor_2, 4 bits wide
  assign and_3_out = B2_2 & A2;  // And and_3, 4 bits wide
  assign xor_3_out = A3 ^ B3;  // XOr xor_3, 4 bits wide
  assign and_4_out = B3 & A3;  // And and_4, 4 bits wide
  assign xor_4_out = A0 ^ B0;  // XOr xor_4, 4 bits wide
  assign and_5_out = and_1_out & xor_1_out;  // And and_5, 4 bits wide
  assign and_6_out = or_1_out & xor_2_out;  // And and_6, 4 bits wide
  assign and_7_out = or_2_out & xor_3_out;  // And and_7, 4 bits wide
  assign xor_5_out = xor_1_out ^ and_1_out;  // XOr xor_5, 4 bits wide
  assign xor_6_out = xor_2_out ^ or_1_out;  // XOr xor_6, 4 bits wide
  assign xor_7_out = xor_3_out ^ or_2_out;  // XOr xor_7, 4 bits wide
  assign or_1_out = and_5_out | and_2_out;  // Or or_1, 4 bits wide
  assign or_2_out = and_6_out | and_3_out;  // Or or_2, 4 bits wide
  assign or_3_out = and_7_out | and_4_out;  // Or or_3, 4 bits wide
  assign or_4_out = xor_4_out | xor_5_out | xor_6_out | xor_7_out;  // Or or_4, 4 bits wide
  Multiplexer #(.Bits(4)) multiplexer_1 (.sel(Control), .in_0(Output), .in_1(or_4_out), .out(multiplexer_1_out));
  D_FF d_ff_1 (.D(multiplexer_1_out[3]), .C(CLK), .Q(Output[3]));  // open: nQ
  D_FF d_ff_2 (.D(multiplexer_1_out[2]), .C(CLK), .Q(Output[2]));  // open: nQ
  D_FF d_ff_3 (.D(multiplexer_1_out[1]), .C(CLK), .Q(Output[1]));  // open: nQ
  D_FF d_ff_4 (.D(multiplexer_1_out[0]), .C(CLK), .Q(Output[0]));  // open: nQ
endmodule
